// Logisim project 332 Register Attempt 2.circ as structural Verilog
module Register_File (
  input  CLR,
  input  [3:0] Read_Reg_1,
  input  [3:0] Read_Reg_2,
  input  [3:0] Write_Reg_RD,
  input  Reg_write,
  input  [15:0] Write_Data,
  input  Clk,
  output [15:0] Read_Data_1,
  output [15:0] Read_Data_2
);

  wire decoder_1_out0, decoder_1_out1, decoder_1_out2, decoder_1_out3, decoder_1_out4, decoder_1_out5,
       decoder_1_out6, decoder_1_out7, decoder_1_out8, decoder_1_out9, decoder_1_out10, decoder_1_out11,
       decoder_1_out12, decoder_1_out13, decoder_1_out14, decoder_1_out15;
  wire [15:0] _0_q, _1_q, _2_q, _3_q, _4_q, _5_q, _6_q, _7_q, _8_q, _9_q, _10_q, _11_q, _12_q, _13_q, _14_q,
       _15_q, and_1_out;

  Decoder #(.select(4)) decoder_1 (
    .out0(decoder_1_out0), .out1(decoder_1_out1), .out2(decoder_1_out2), .out3(decoder_1_out3),
    .out4(decoder_1_out4), .out5(decoder_1_out5), .out6(decoder_1_out6), .out7(decoder_1_out7),
    .out8(decoder_1_out8), .out9(decoder_1_out9), .out10(decoder_1_out10), .out11(decoder_1_out11),
    .out12(decoder_1_out12), .out13(decoder_1_out13), .out14(decoder_1_out14), .out15(decoder_1_out15),
    .sel(Write_Reg_RD));  // open: en
  and and_1 (and_1_out[0], decoder_1_out0, Reg_write);
  and and_2 (and_1_out[1], decoder_1_out1, Reg_write);
  and and_3 (and_1_out[2], decoder_1_out2, Reg_write);
  and and_4 (and_1_out[3], decoder_1_out3, Reg_write);
  and and_5 (and_1_out[4], decoder_1_out4, Reg_write);
  and and_6 (and_1_out[5], decoder_1_out5, Reg_write);
  and and_7 (and_1_out[6], decoder_1_out6, Reg_write);
  and and_8 (and_1_out[7], decoder_1_out7, Reg_write);
  and and_9 (and_1_out[8], decoder_1_out8, Reg_write);
  and and_10 (and_1_out[9], decoder_1_out9, Reg_write);
  and and_11 (and_1_out[10], decoder_1_out10, Reg_write);
  and and_12 (and_1_out[11], decoder_1_out11, Reg_write);
  and and_13 (and_1_out[12], decoder_1_out12, Reg_write);
  and and_14 (and_1_out[13], decoder_1_out13, Reg_write);
  and and_15 (and_1_out[14], decoder_1_out14, Reg_write);
  and and_16 (and_1_out[15], decoder_1_out15, Reg_write);
  Register #(.width(16)) _0 (.D(Write_Data), .en(and_1_out[0]), .Q(_0_q), .clk(Clk), .clr(CLR));
  Register #(.width(16)) _1 (.D(Write_Data), .en(and_1_out[1]), .Q(_1_q), .clk(Clk), .clr(CLR));
  Register #(.width(16)) _2 (.D(Write_Data), .en(and_1_out[2]), .Q(_2_q), .clk(Clk), .clr(CLR));
  Register #(.width(16)) _3 (.D(Write_Data), .en(and_1_out[3]), .Q(_3_q), .clk(Clk), .clr(CLR));
  Register #(.width(16)) _4 (.D(Write_Data), .en(and_1_out[4]), .Q(_4_q), .clk(Clk), .clr(CLR));
  Register #(.width(16)) _5 (.D(Write_Data), .en(and_1_out[5]), .Q(_5_q), .clk(Clk), .clr(CLR));
  Register #(.width(16)) _6 (.D(Write_Data), .en(and_1_out[6]), .Q(_6_q), .clk(Clk), .clr(CLR));
  Register #(.width(16)) _7 (.D(Write_Data), .en(and_1_out[7]), .Q(_7_q), .clk(Clk), .clr(CLR));
  Register #(.width(16)) _8 (.D(Write_Data), .en(and_1_out[8]), .Q(_8_q), .clk(Clk), .clr(CLR));
  Register #(.width(16)) _9 (.D(Write_Data), .en(and_1_out[9]), .Q(_9_q), .clk(Clk), .clr(CLR));
  Register #(.width(16)) _10 (.D(Write_Data), .en(and_1_out[10]), .Q(_10_q), .clk(Clk), .clr(CLR));
  Register #(.width(16)) _11 (.D(Write_Data), .en(and_1_out[11]), .Q(_11_q), .clk(Clk), .clr(CLR));
  Register #(.width(16)) _12 (.D(Write_Data), .en(and_1_out[12]), .Q(_12_q), .clk(Clk), .clr(CLR));
  Register #(.width(16)) _13 (.D(Write_Data), .en(and_1_out[13]), .Q(_13_q), .clk(Clk), .clr(CLR));
  Register #(.width(16)) _14 (.D(Write_Data), .en(and_1_out[14]), .Q(_14_q), .clk(Clk), .clr(CLR));
  Register #(.width(16)) _15 (.D(Write_Data), .en(and_1_out[15]), .Q(_15_q), .clk(Clk), .clr(CLR));
  Multiplexer #(.select(4), .width(16)) multiplexer_1 (
    .in0(_0_q), .in1(_1_q), .in2(_2_q), .in3(_3_q), .in4(_4_q), .in5(_5_q), .in6(_6_q), .in7(_7_q),
    .in8(_8_q), .in9(_9_q), .in10(_10_q), .in11(_11_q), .in12(_12_q), .in13(_13_q), .in14(_14_q),
    .in15(_15_q), .out(Read_Data_1), .sel(Read_Reg_1));  // open: en
  Multiplexer #(.select(4), .width(16)) multiplexer_2 (
    .in0(_0_q), .in1(_1_q), .in2(_2_q), .in3(_3_q), .in4(_4_q), .in5(_5_q), .in6(_6_q), .in7(_7_q),
    .in8(_8_q), .in9(_9_q), .in10(_10_q), .in11(_11_q), .in12(_12_q), .in13(_13_q), .in14(_14_q),
    .in15(_15_q), .out(Read_Data_2), .sel(Read_Reg_2));  // open: en
endmodule
